# Fritzing sketch traffic light (saved by Fritzing 0.9.4)
breadboards: 1

parts:
  LED1 = LED - 5mm [color="Green (565nm)" package="5 mm [THT]"]
  LED2 = LED - 5mm [color="Green (565nm)" package="5 mm [THT]"]
  LED3 = LED - 5mm [color="Green (565nm)" package="5 mm [THT]"]
  R1 = Resistor [tolerance=±5% resistance=220 package="2512 [SMD]"]
  R2 = Resistor [tolerance=±5% resistance=220 package="2512 [SMD]"]
  R3 = Resistor [tolerance=±5% resistance=220 package="2512 [SMD]"]
  Part1 = Arduino Uno (Rev3) - ICSP

nets:
  N1: LED1.cathode, R1.Pin_1
  N2: LED1.anode, Part1.D5_PWM
  N3: LED2.cathode, R2.Pin_1
  N4: LED2.anode, Part1.D7
  N5: LED3.cathode, R3.Pin_1
  N6: LED3.anode, Part1.D3_PWM
  N7: R1.Pin_0, R2.Pin_0, R3.Pin_0, Part1.GND
